// Digital circuit connection_box.dig as structural Verilog
module connection_box (
  input  in,
  input  Si,
  input  clk,
  output u0,
  output d0,
  output u1,
  output d1,
  output u2,
  output d2,
  output u3,
  output d3,
  output So
);

  wire [3:0] shift_reg_4bit_1_d;

  shift_reg_4bit shift_reg_4bit_1 (.i(Si), .c(clk), .o(So), .d(shift_reg_4bit_1_d));
  NFET nfet_1 (.G(shift_reg_4bit_1_d[0]), .D(in), .S(d0));
  NFET nfet_2 (.G(shift_reg_4bit_1_d[1]), .D(in), .S(d1));
  NFET nfet_3 (.G(shift_reg_4bit_1_d[2]), .D(in), .S(d2));
  NFET nfet_4 (.G(shift_reg_4bit_1_d[3]), .D(in), .S(d3));

  assign u0 = d0;
  assign u1 = d1;
  assign u2 = d2;
  assign u3 = d3;
endmodule
