// Digital circuit fpga_ckt.dig as structural Verilog
module fpga_ckt (
  input  clk,
  input  p0,
  input  p1,
  input  p2,
  input  p3,
  input  p4,
  input  p5,
  input  p6,
  input  p7,
  input  p8,
  input  p9,
  input  p10,
  input  p11,
  input  p12,
  input  p13,
  input  p14,
  input  p15,
  input  p16,
  input  p17,
  input  p18,
  input  p19,
  input  p20,
  input  p21,
  input  p22,
  input  p23
);

  wire connection_box_1_p3, connection_box_1_p5, connection_box_1_p6, connection_box_1_p7,
       connection_box_1_p8, connection_box_1_p10, connection_box_1_p11, connection_box_2_p3,
       connection_box_2_p6, connection_box_2_p8, connection_box_2_p11, connection_box_3_p3,
       connection_box_3_p5, connection_box_3_p6, connection_box_3_p7, connection_box_3_p8,
       connection_box_3_p10, connection_box_3_p11, connection_box_4_p3, connection_box_4_p6,
       connection_box_4_p8, connection_box_4_p11, connection_box_5_p3, connection_box_5_p5,
       connection_box_5_p6, connection_box_5_p7, connection_box_5_p8, connection_box_5_p10,
       connection_box_5_p11, connection_box_6_p3, connection_box_6_p6, connection_box_6_p8,
       connection_box_6_p11, connection_box_7_p10, connection_box_7_p11, connection_box_8_p7,
       connection_box_8_p10, connection_box_9_p8, connection_box_9_p9, connection_box_9_p10,
       connection_box_10_p2, connection_box_10_p10, connection_box_10_p11, connection_box_10_p12,
       connection_box_11_p3, connection_box_11_p5, connection_box_11_p6, connection_box_11_p7,
       connection_box_11_p8, connection_box_11_p10, connection_box_11_p11, connection_box_12_p2,
       connection_box_12_p5, connection_box_12_p8, connection_box_12_p10, connection_box_12_p13,
       connection_box_13_p3, connection_box_13_p5, connection_box_13_p6, connection_box_13_p7,
       connection_box_13_p8, connection_box_13_p10, connection_box_13_p11, connection_box_14_p2,
       connection_box_14_p5, connection_box_14_p8, connection_box_14_p10, connection_box_14_p13,
       connection_box_15_p3, connection_box_15_p5, connection_box_15_p6, connection_box_15_p7,
       connection_box_15_p8, connection_box_15_p10, connection_box_15_p11, connection_box_16_p1,
       connection_box_16_p4, connection_box_16_p7, connection_box_16_p9, connection_box_16_p12,
       connection_box_17_p10, connection_box_17_p11, connection_box_18_p7, connection_box_18_p10,
       connection_box_19_p8, connection_box_19_p9, connection_box_19_p10, connection_box_20_p2,
       connection_box_20_p10, connection_box_20_p11, connection_box_20_p12, connection_box_21_p3,
       connection_box_21_p5, connection_box_21_p6, connection_box_21_p7, connection_box_21_p8,
       connection_box_21_p10, connection_box_21_p11, connection_box_22_p2, connection_box_22_p5,
       connection_box_22_p8, connection_box_22_p10, connection_box_22_p13, connection_box_23_p3,
       connection_box_23_p5, connection_box_23_p6, connection_box_23_p7, connection_box_23_p8,
       connection_box_23_p10, connection_box_23_p11, connection_box_24_p2, connection_box_24_p5,
       connection_box_24_p8, connection_box_24_p10, connection_box_24_p13, connection_box_25_p3,
       connection_box_25_p5, connection_box_25_p6, connection_box_25_p7, connection_box_25_p8,
       connection_box_25_p10, connection_box_25_p11, connection_box_26_p1, connection_box_26_p4,
       connection_box_26_p7, connection_box_26_p9, connection_box_26_p12, connection_box_27_p10,
       connection_box_27_p11, connection_box_28_p7, connection_box_28_p10, connection_box_29_p8,
       connection_box_29_p9, connection_box_29_p10, connection_box_30_p2, connection_box_30_p10,
       connection_box_30_p11, connection_box_30_p12, connection_box_31_p3, connection_box_31_p5,
       connection_box_31_p7, connection_box_31_p11, connection_box_31_p12, connection_box_31_p14,
       connection_box_32_p2, connection_box_32_p5, connection_box_32_p7, connection_box_32_p8,
       connection_box_33_p3, connection_box_33_p5, connection_box_33_p7, connection_box_33_p11,
       connection_box_33_p12, connection_box_33_p14, connection_box_34_p2, connection_box_34_p5,
       connection_box_34_p7, connection_box_34_p8, connection_box_35_p3, connection_box_35_p5,
       connection_box_35_p7, connection_box_35_p11, connection_box_35_p12, connection_box_35_p14,
       connection_box_36_p1, connection_box_36_p4, connection_box_36_p6, connection_box_36_p7,
       connection_box_37_p1, connection_box_37_p3, connection_box_37_p5, connection_box_37_p10,
       connection_box_37_p12, connection_box_38_p2, connection_box_38_p7, connection_box_39_p1,
       connection_box_39_p3, connection_box_39_p5, connection_box_39_p10, connection_box_39_p12,
       connection_box_40_p2, connection_box_40_p7, connection_box_41_p1, connection_box_41_p3,
       connection_box_41_p5, connection_box_41_p10, connection_box_41_p12, connection_box_42_p2,
       connection_box_42_p7, p0_t, p1_t, p2_t, p3_t, p4_t, p5_t, p6_t, p7_t, p8_t, p9_t, p10_t, p11_t, p12_t,
       p13_t, p14_t, p15_t, p16_t, p17_t, p18_t, p19_t, p20_t, p21_t, p22_t, p23_t, slice_block_1_p12,
       slice_block_1_p14, slice_block_1_p17, slice_block_1_p18, slice_block_2_p17, slice_block_3_p9,
       slice_block_3_p12, slice_block_3_p16, slice_block_4_p12, slice_block_4_p14, slice_block_4_p17,
       slice_block_4_p18, slice_block_5_p17, slice_block_6_p9, slice_block_6_p12, slice_block_6_p16,
       slice_block_7_p12, slice_block_7_p14, slice_block_7_p17, slice_block_7_p18, slice_block_8_p17,
       slice_block_9_p9, slice_block_9_p12, slice_block_9_p16, switch_block_1_d, switch_block_1_r,
       switch_block_2_d, switch_block_2_r, switch_block_3_d, switch_block_3_r, switch_block_4_r,
       switch_block_5_r, switch_block_6_r, switch_block_7_r, switch_block_8_r, switch_block_9_r,
       switch_block_10_r, switch_block_11_r, switch_block_12_r, switch_block_13_r, switch_block_14_r,
       switch_block_15_r, switch_block_16_r, switch_block_17_d, switch_block_17_r, switch_block_18_d,
       switch_block_18_r, switch_block_19_d, switch_block_19_r, switch_block_20_r, switch_block_21_r,
       switch_block_22_r, switch_block_23_r, switch_block_24_r, switch_block_25_r, switch_block_26_r,
       switch_block_27_r, switch_block_28_r, switch_block_29_r, switch_block_30_r, switch_block_31_r,
       switch_block_32_r, switch_block_33_d, switch_block_33_r, switch_block_34_d, switch_block_34_r,
       switch_block_35_d, switch_block_35_r, switch_block_36_r, switch_block_37_r, switch_block_38_r,
       switch_block_39_r, switch_block_40_r, switch_block_41_r, switch_block_42_r, switch_block_43_r,
       switch_block_44_r, switch_block_45_r, switch_block_46_r, switch_block_47_r, switch_block_48_r,
       switch_block_49_d, switch_block_50_d, switch_block_51_d, switch_block_58_u, switch_block_59_u,
       switch_block_60_u, switch_block_61_d, switch_block_62_d, switch_block_62_u, switch_block_63_d,
       switch_block_63_u, switch_block_64_u;
  wire [3:0] c0, c1, c2, c3, c4, c5, c6, c7, c8, c9, c10, c11, c12, c13, c14, c15, c16, c17, c18, c19, c20,
       c21, c22, c23, c24, c25, c26, c27, c28, c29, c30, c31, c32, c33, c34, c35, c36, c37, c38, c39, c40,
       c41;
  wire [5:0] s00, s01, s02, s03, s10, s11, s12, s13, s20, s21, s22, s23, s30, s31, s32, s33, s40, s41, s42,
       s43, s50, s51, s52, s53, s60, s61, s62, s63, s70, s71, s72, s73, s80, s81, s82, s83, s90, s91, s92,
       s93, s100, s101, s102, s103, s110, s111, s112, s113, s120, s121, s122, s123, s130, s131, s132, s133,
       s140, s141, s142, s143, s150, s151, s152, s153;
  wire [32:0] d0, d1, d2, d3, d4, d5, d6, d7, d8;

  switch_block switch_block_1 (.R(switch_block_1_r), .D(switch_block_1_d), .clk(clk), .cfg(s03));  // open: L, U
  // connection_box connection_box_1: pin names not known; wires that end beside it: p0, switch_block_1_d, connection_box_1_p3, c0, connection_box_1_p5, connection_box_1_p6, connection_box_1_p7, connection_box_1_p8, clk, connection_box_1_p10, connection_box_1_p11
  // connection_box connection_box_2: pin names not known; wires that end beside it: p1, connection_box_1_p3, connection_box_2_p3, c1, connection_box_1_p6, connection_box_2_p6, connection_box_1_p8, connection_box_2_p8, clk, connection_box_1_p11, connection_box_2_p11
  switch_block switch_block_2 (
    .R(switch_block_2_r), .U(connection_box_2_p3), .D(switch_block_2_d), .clk(clk), .cfg(s43));  // open: L
  // connection_box connection_box_3: pin names not known; wires that end beside it: p2, switch_block_2_d, connection_box_3_p3, c2, connection_box_3_p5, connection_box_3_p6, connection_box_3_p7, connection_box_3_p8, clk, connection_box_3_p10, connection_box_3_p11
  // connection_box connection_box_4: pin names not known; wires that end beside it: p3, connection_box_3_p3, connection_box_4_p3, c3, connection_box_3_p6, connection_box_4_p6, connection_box_3_p8, connection_box_4_p8, clk, connection_box_3_p11, connection_box_4_p11
  switch_block switch_block_3 (
    .R(switch_block_3_r), .U(connection_box_4_p3), .D(switch_block_3_d), .clk(clk), .cfg(s83));  // open: L
  // connection_box connection_box_5: pin names not known; wires that end beside it: p4, switch_block_3_d, connection_box_5_p3, c4, connection_box_5_p5, connection_box_5_p6, connection_box_5_p7, connection_box_5_p8, clk, connection_box_5_p10, connection_box_5_p11
  // connection_box connection_box_6: pin names not known; wires that end beside it: p5, connection_box_5_p3, connection_box_6_p3, c5, connection_box_5_p6, connection_box_6_p6, connection_box_5_p8, connection_box_6_p8, clk, connection_box_5_p11, connection_box_6_p11
  switch_block switch_block_4 (.R(switch_block_4_r), .U(connection_box_6_p3), .clk(clk), .cfg(s123));  // open: L, D
  switch_block switch_block_5 (.R(switch_block_5_r), .D(connection_box_1_p5), .clk(clk), .cfg(s02));  // open: L, U
  switch_block switch_block_6 (
    .R(switch_block_6_r), .U(connection_box_2_p6), .D(connection_box_3_p5), .clk(clk), .cfg(s42));  // open: L
  switch_block switch_block_7 (
    .R(switch_block_7_r), .U(connection_box_4_p6), .D(connection_box_5_p5), .clk(clk), .cfg(s82));  // open: L
  switch_block switch_block_8 (.R(switch_block_8_r), .U(connection_box_6_p6), .clk(clk), .cfg(s122));  // open: L, D
  ROM #(.AddrBits(1), .Bits(24)) io_cfg (
    .A(1'b0), .sel(1'b1),
    .D({p23_t, p22_t, p21_t, p20_t, p19_t, p18_t, p17_t, p16_t, p15_t, p14_t, p13_t, p12_t, p11_t, p10_t, p9_t, p8_t, p7_t, p6_t, p5_t, p4_t, p3_t, p2_t, p1_t, p0_t}));
  ROM #(.AddrBits(1), .Bits(48)) sw_cfg0 (.A(1'b0), .sel(1'b1), .D({s13, s12, s11, s10, s03, s02, s01, s00}));
  ROM #(.AddrBits(1), .Bits(48)) sw_cfg2 (.A(1'b0), .sel(1'b1), .D({s53, s52, s51, s50, s43, s42, s41, s40}));
  ROM #(.AddrBits(1), .Bits(48)) sw_cfg4 (.A(1'b0), .sel(1'b1), .D({s93, s92, s91, s90, s83, s82, s81, s80}));
  ROM #(.AddrBits(1), .Bits(48)) sw_cfg6 (.A(1'b0), .sel(1'b1), .D({s133, s132, s131, s130, s123, s122, s121, s120}));
  switch_block switch_block_9 (.R(switch_block_9_r), .D(connection_box_1_p7), .clk(clk), .cfg(s01));  // open: L, U
  switch_block switch_block_10 (
    .R(switch_block_10_r), .U(connection_box_2_p8), .D(connection_box_3_p7), .clk(clk), .cfg(s41));  // open: L
  switch_block switch_block_11 (
    .R(switch_block_11_r), .U(connection_box_4_p8), .D(connection_box_5_p7), .clk(clk), .cfg(s81));  // open: L
  switch_block switch_block_12 (.R(switch_block_12_r), .U(connection_box_6_p8), .clk(clk), .cfg(s121));  // open: L, D
  switch_block switch_block_13 (.R(switch_block_13_r), .D(connection_box_1_p10), .clk(clk), .cfg(s00));  // open: L, U
  switch_block switch_block_14 (
    .R(switch_block_14_r), .U(connection_box_2_p11), .D(connection_box_3_p10), .clk(clk), .cfg(s40));  // open: L
  switch_block switch_block_15 (
    .R(switch_block_15_r), .U(connection_box_4_p11), .D(connection_box_5_p10), .clk(clk), .cfg(s80));  // open: L
  switch_block switch_block_16 (.R(switch_block_16_r), .U(connection_box_6_p11), .clk(clk), .cfg(s120));  // open: L, D
  ROM #(.AddrBits(1), .Bits(48)) sw_cfg1 (.A(1'b0), .sel(1'b1), .D({s33, s32, s31, s30, s23, s22, s21, s20}));
  ROM #(.AddrBits(1), .Bits(48)) sw_cfg3 (.A(1'b0), .sel(1'b1), .D({s73, s72, s71, s70, s63, s62, s61, s60}));
  ROM #(.AddrBits(1), .Bits(48)) sw_cfg5 (.A(1'b0), .sel(1'b1), .D({s113, s112, s111, s110, s103, s102, s101, s100}));
  ROM #(.AddrBits(1), .Bits(48)) sw_cfg7 (.A(1'b0), .sel(1'b1), .D({s153, s152, s151, s150, s143, s142, s141, s140}));
  // slice_block slice_block_1: pin names not known; wires that end beside it: connection_box_1_p10, connection_box_1_p8, connection_box_1_p6, connection_box_1_p3, switch_block_14_r, switch_block_10_r, switch_block_6_r, switch_block_1_r, switch_block_13_r, switch_block_14_r, d0, slice_block_1_p12, switch_block_10_r, slice_block_1_p14, switch_block_6_r, clk, slice_block_1_p17, slice_block_1_p18
  // slice_block slice_block_2: pin names not known; wires that end beside it: connection_box_3_p10, connection_box_3_p8, connection_box_3_p6, connection_box_3_p3, switch_block_15_r, switch_block_11_r, switch_block_7_r, switch_block_14_r, switch_block_15_r, d3, switch_block_10_r, switch_block_11_r, switch_block_6_r, switch_block_7_r, clk, switch_block_2_r, slice_block_2_p17
  // slice_block slice_block_3: pin names not known; wires that end beside it: connection_box_5_p10, connection_box_5_p8, connection_box_5_p6, connection_box_5_p3, switch_block_16_r, switch_block_12_r, switch_block_8_r, switch_block_15_r, slice_block_3_p9, d6, switch_block_11_r, slice_block_3_p12, switch_block_7_r, clk, switch_block_3_r, slice_block_3_p16
  // connection_box connection_box_7: pin names not known; wires that end beside it: switch_block_16_r, switch_block_12_r, switch_block_8_r, switch_block_4_r, clk, c6, p6, slice_block_3_p9, slice_block_3_p12, connection_box_7_p10, connection_box_7_p11
  // connection_box connection_box_8: pin names not known; wires that end beside it: switch_block_13_r, switch_block_9_r, switch_block_5_r, p23, c23, clk, connection_box_8_p7, slice_block_1_p12, slice_block_1_p14, connection_box_8_p10
  // connection_box connection_box_9: pin names not known; wires that end beside it: connection_box_8_p7, slice_block_1_p12, slice_block_1_p14, connection_box_8_p10, p22, c22, clk, connection_box_9_p8, connection_box_9_p9, connection_box_9_p10, slice_block_1_p17
  // connection_box connection_box_10: pin names not known; wires that end beside it: connection_box_7_p10, connection_box_10_p2, slice_block_3_p9, slice_block_3_p12, connection_box_7_p10, connection_box_7_p11, clk, c7, p7, connection_box_10_p10, connection_box_10_p11, connection_box_10_p12, connection_box_10_p2
  switch_block switch_block_17 (
    .R(switch_block_17_r), .L(slice_block_1_p17), .D(switch_block_17_d), .clk(clk), .cfg(s13));  // open: U
  // connection_box connection_box_11: pin names not known; wires that end beside it: slice_block_1_p18, switch_block_17_d, connection_box_11_p3, c24, connection_box_11_p5, connection_box_11_p6, connection_box_11_p7, connection_box_11_p8, clk, connection_box_11_p10, connection_box_11_p11
  // connection_box connection_box_12: pin names not known; wires that end beside it: switch_block_2_r, connection_box_12_p2, connection_box_12_p2, connection_box_11_p3, connection_box_12_p5, c25, connection_box_11_p6, connection_box_12_p8, connection_box_11_p8, connection_box_12_p10, clk, connection_box_11_p11, connection_box_12_p13
  switch_block switch_block_18 (
    .R(switch_block_18_r), .L(switch_block_2_r), .U(connection_box_12_p5), .D(switch_block_18_d), .clk(clk),
    .cfg(s53));
  // connection_box connection_box_13: pin names not known; wires that end beside it: slice_block_2_p17, switch_block_18_d, connection_box_13_p3, c30, connection_box_13_p5, connection_box_13_p6, connection_box_13_p7, connection_box_13_p8, clk, connection_box_13_p10, connection_box_13_p11
  // connection_box connection_box_14: pin names not known; wires that end beside it: switch_block_3_r, connection_box_14_p2, connection_box_14_p2, connection_box_13_p3, connection_box_14_p5, c31, connection_box_13_p6, connection_box_14_p8, connection_box_13_p8, connection_box_14_p10, clk, connection_box_13_p11, connection_box_14_p13
  switch_block switch_block_19 (
    .R(switch_block_19_r), .L(switch_block_3_r), .U(connection_box_14_p5), .D(switch_block_19_d), .clk(clk),
    .cfg(s93));
  // connection_box connection_box_15: pin names not known; wires that end beside it: slice_block_3_p16, switch_block_19_d, connection_box_15_p3, c36, connection_box_15_p5, connection_box_15_p6, connection_box_15_p7, connection_box_15_p8, clk, connection_box_15_p10, connection_box_15_p11
  // connection_box connection_box_16: pin names not known; wires that end beside it: connection_box_16_p1, connection_box_16_p1, connection_box_15_p3, connection_box_16_p4, c37, connection_box_15_p6, connection_box_16_p7, connection_box_15_p8, connection_box_16_p9, clk, connection_box_15_p11, connection_box_16_p12
  switch_block switch_block_20 (
    .R(switch_block_20_r), .L(connection_box_10_p2), .U(connection_box_16_p4), .clk(clk), .cfg(s133));  // open: D
  ROM #(.AddrBits(1), .Bits(64)) conn_cfg0 (
    .A(1'b0), .sel(1'b1), .D({c15, c14, c13, c12, c11, c10, c9, c8, c7, c6, c5, c4, c3, c2, c1, c0}));
  ROM #(.AddrBits(1), .Bits(64)) conn_cfg1 (
    .A(1'b0), .sel(1'b1), .D({c31, c30, c29, c28, c27, c26, c25, c24, c23, c22, c21, c20, c19, c18, c17, c16}));
  ROM #(.AddrBits(1), .Bits(40)) conn_cfg2 (
    .A(1'b0), .sel(1'b1), .D({c41, c40, c39, c38, c37, c36, c35, c34, c33, c32}));
  ROM #(.AddrBits(1), .Bits(33)) slice_cfg0 (.A(1'b0), .sel(1'b1), .D(d0));
  ROM #(.AddrBits(1), .Bits(33)) slice_cfg1 (.A(1'b0), .sel(1'b1), .D(d1));
  ROM #(.AddrBits(1), .Bits(33)) slice_cfg2 (.A(1'b0), .sel(1'b1), .D(d2));
  switch_block switch_block_21 (
    .R(switch_block_21_r), .L(connection_box_9_p10), .D(connection_box_11_p5), .clk(clk), .cfg(s12));  // open: U
  switch_block switch_block_22 (
    .R(switch_block_22_r), .L(switch_block_6_r), .U(connection_box_12_p8), .D(connection_box_13_p5),
    .clk(clk), .cfg(s52));
  switch_block switch_block_23 (
    .R(switch_block_23_r), .L(switch_block_7_r), .U(connection_box_14_p8), .D(connection_box_15_p5),
    .clk(clk), .cfg(s92));
  switch_block switch_block_24 (
    .R(switch_block_24_r), .L(connection_box_10_p12), .U(connection_box_16_p7), .clk(clk), .cfg(s132));  // open: D
  switch_block switch_block_25 (
    .R(switch_block_25_r), .L(connection_box_9_p9), .D(connection_box_11_p7), .clk(clk), .cfg(s11));  // open: U
  switch_block switch_block_26 (
    .R(switch_block_26_r), .L(switch_block_10_r), .U(connection_box_12_p10), .D(connection_box_13_p7),
    .clk(clk), .cfg(s51));
  switch_block switch_block_27 (
    .R(switch_block_27_r), .L(switch_block_11_r), .U(connection_box_14_p10), .D(connection_box_15_p7),
    .clk(clk), .cfg(s91));
  switch_block switch_block_28 (
    .R(switch_block_28_r), .L(connection_box_10_p11), .U(connection_box_16_p9), .clk(clk), .cfg(s131));  // open: D
  ROM #(.AddrBits(1), .Bits(33)) slice_cfg3 (.A(1'b0), .sel(1'b1), .D(d3));
  ROM #(.AddrBits(1), .Bits(33)) slice_cfg4 (.A(1'b0), .sel(1'b1), .D(d4));
  ROM #(.AddrBits(1), .Bits(33)) slice_cfg5 (.A(1'b0), .sel(1'b1), .D(d5));
  switch_block switch_block_29 (
    .R(switch_block_29_r), .L(connection_box_9_p8), .D(connection_box_11_p10), .clk(clk), .cfg(s10));  // open: U
  switch_block switch_block_30 (
    .R(switch_block_30_r), .L(switch_block_14_r), .U(connection_box_12_p13), .D(connection_box_13_p10),
    .clk(clk), .cfg(s50));
  switch_block switch_block_31 (
    .R(switch_block_31_r), .L(switch_block_15_r), .U(connection_box_14_p13), .D(connection_box_15_p10),
    .clk(clk), .cfg(s90));
  switch_block switch_block_32 (
    .R(switch_block_32_r), .L(connection_box_10_p10), .U(connection_box_16_p12), .clk(clk), .cfg(s130));  // open: D
  ROM #(.AddrBits(1), .Bits(33)) slice_cfg6 (.A(1'b0), .sel(1'b1), .D(d6));
  ROM #(.AddrBits(1), .Bits(33)) slice_cfg7 (.A(1'b0), .sel(1'b1), .D(d7));
  ROM #(.AddrBits(1), .Bits(33)) slice_cfg8 (.A(1'b0), .sel(1'b1), .D(d8));
  // slice_block slice_block_4: pin names not known; wires that end beside it: connection_box_11_p10, connection_box_11_p8, connection_box_11_p6, connection_box_11_p3, switch_block_30_r, switch_block_26_r, switch_block_22_r, switch_block_17_r, switch_block_29_r, switch_block_30_r, d1, slice_block_4_p12, switch_block_26_r, slice_block_4_p14, switch_block_22_r, clk, slice_block_4_p17, slice_block_4_p18
  // slice_block slice_block_5: pin names not known; wires that end beside it: connection_box_13_p10, connection_box_13_p8, connection_box_13_p6, connection_box_13_p3, switch_block_31_r, switch_block_27_r, switch_block_23_r, switch_block_30_r, switch_block_31_r, d4, switch_block_26_r, switch_block_27_r, switch_block_22_r, switch_block_23_r, clk, switch_block_18_r, slice_block_5_p17
  // slice_block slice_block_6: pin names not known; wires that end beside it: connection_box_15_p10, connection_box_15_p8, connection_box_15_p6, connection_box_15_p3, switch_block_32_r, switch_block_28_r, switch_block_24_r, switch_block_31_r, slice_block_6_p9, d7, switch_block_27_r, slice_block_6_p12, switch_block_23_r, clk, switch_block_19_r, slice_block_6_p16
  // connection_box connection_box_17: pin names not known; wires that end beside it: switch_block_32_r, switch_block_28_r, switch_block_24_r, switch_block_20_r, clk, c8, p8, slice_block_6_p9, slice_block_6_p12, connection_box_17_p10, connection_box_17_p11
  // connection_box connection_box_18: pin names not known; wires that end beside it: switch_block_29_r, switch_block_25_r, switch_block_21_r, p21, c21, clk, connection_box_18_p7, slice_block_4_p12, slice_block_4_p14, connection_box_18_p10
  // connection_box connection_box_19: pin names not known; wires that end beside it: connection_box_18_p7, slice_block_4_p12, slice_block_4_p14, connection_box_18_p10, p20, c20, clk, connection_box_19_p8, connection_box_19_p9, connection_box_19_p10, slice_block_4_p17
  // connection_box connection_box_20: pin names not known; wires that end beside it: connection_box_17_p10, connection_box_20_p2, slice_block_6_p9, slice_block_6_p12, connection_box_17_p10, connection_box_17_p11, clk, c9, p9, connection_box_20_p10, connection_box_20_p11, connection_box_20_p12, connection_box_20_p2
  switch_block switch_block_33 (
    .R(switch_block_33_r), .L(slice_block_4_p17), .D(switch_block_33_d), .clk(clk), .cfg(s23));  // open: U
  // connection_box connection_box_21: pin names not known; wires that end beside it: slice_block_4_p18, switch_block_33_d, connection_box_21_p3, c26, connection_box_21_p5, connection_box_21_p6, connection_box_21_p7, connection_box_21_p8, clk, connection_box_21_p10, connection_box_21_p11
  // connection_box connection_box_22: pin names not known; wires that end beside it: switch_block_18_r, connection_box_22_p2, connection_box_22_p2, connection_box_21_p3, connection_box_22_p5, c27, connection_box_21_p6, connection_box_22_p8, connection_box_21_p8, connection_box_22_p10, clk, connection_box_21_p11, connection_box_22_p13
  switch_block switch_block_34 (
    .R(switch_block_34_r), .L(switch_block_18_r), .U(connection_box_22_p5), .D(switch_block_34_d), .clk(clk),
    .cfg(s63));
  // connection_box connection_box_23: pin names not known; wires that end beside it: slice_block_5_p17, switch_block_34_d, connection_box_23_p3, c32, connection_box_23_p5, connection_box_23_p6, connection_box_23_p7, connection_box_23_p8, clk, connection_box_23_p10, connection_box_23_p11
  // connection_box connection_box_24: pin names not known; wires that end beside it: switch_block_19_r, connection_box_24_p2, connection_box_24_p2, connection_box_23_p3, connection_box_24_p5, c33, connection_box_23_p6, connection_box_24_p8, connection_box_23_p8, connection_box_24_p10, clk, connection_box_23_p11, connection_box_24_p13
  switch_block switch_block_35 (
    .R(switch_block_35_r), .L(switch_block_19_r), .U(connection_box_24_p5), .D(switch_block_35_d), .clk(clk),
    .cfg(s103));
  // connection_box connection_box_25: pin names not known; wires that end beside it: slice_block_6_p16, switch_block_35_d, connection_box_25_p3, c38, connection_box_25_p5, connection_box_25_p6, connection_box_25_p7, connection_box_25_p8, clk, connection_box_25_p10, connection_box_25_p11
  // connection_box connection_box_26: pin names not known; wires that end beside it: connection_box_26_p1, connection_box_26_p1, connection_box_25_p3, connection_box_26_p4, c39, connection_box_25_p6, connection_box_26_p7, connection_box_25_p8, connection_box_26_p9, clk, connection_box_25_p11, connection_box_26_p12
  switch_block switch_block_36 (
    .R(switch_block_36_r), .L(connection_box_20_p2), .U(connection_box_26_p4), .clk(clk), .cfg(s143));  // open: D
  switch_block switch_block_37 (
    .R(switch_block_37_r), .L(connection_box_19_p10), .D(connection_box_21_p5), .clk(clk), .cfg(s22));  // open: U
  switch_block switch_block_38 (
    .R(switch_block_38_r), .L(switch_block_22_r), .U(connection_box_22_p8), .D(connection_box_23_p5),
    .clk(clk), .cfg(s62));
  switch_block switch_block_39 (
    .R(switch_block_39_r), .L(switch_block_23_r), .U(connection_box_24_p8), .D(connection_box_25_p5),
    .clk(clk), .cfg(s102));
  switch_block switch_block_40 (
    .R(switch_block_40_r), .L(connection_box_20_p12), .U(connection_box_26_p7), .clk(clk), .cfg(s142));  // open: D
  switch_block switch_block_41 (
    .R(switch_block_41_r), .L(connection_box_19_p9), .D(connection_box_21_p7), .clk(clk), .cfg(s21));  // open: U
  switch_block switch_block_42 (
    .R(switch_block_42_r), .L(switch_block_26_r), .U(connection_box_22_p10), .D(connection_box_23_p7),
    .clk(clk), .cfg(s61));
  switch_block switch_block_43 (
    .R(switch_block_43_r), .L(switch_block_27_r), .U(connection_box_24_p10), .D(connection_box_25_p7),
    .clk(clk), .cfg(s101));
  switch_block switch_block_44 (
    .R(switch_block_44_r), .L(connection_box_20_p11), .U(connection_box_26_p9), .clk(clk), .cfg(s141));  // open: D
  switch_block switch_block_45 (
    .R(switch_block_45_r), .L(connection_box_19_p8), .D(connection_box_21_p10), .clk(clk), .cfg(s20));  // open: U
  switch_block switch_block_46 (
    .R(switch_block_46_r), .L(switch_block_30_r), .U(connection_box_22_p13), .D(connection_box_23_p10),
    .clk(clk), .cfg(s60));
  switch_block switch_block_47 (
    .R(switch_block_47_r), .L(switch_block_31_r), .U(connection_box_24_p13), .D(connection_box_25_p10),
    .clk(clk), .cfg(s100));
  switch_block switch_block_48 (
    .R(switch_block_48_r), .L(connection_box_20_p10), .U(connection_box_26_p12), .clk(clk), .cfg(s140));  // open: D
  // slice_block slice_block_7: pin names not known; wires that end beside it: connection_box_21_p10, connection_box_21_p8, connection_box_21_p6, connection_box_21_p3, switch_block_46_r, switch_block_42_r, switch_block_38_r, switch_block_33_r, switch_block_45_r, switch_block_46_r, d2, slice_block_7_p12, switch_block_42_r, slice_block_7_p14, switch_block_38_r, clk, slice_block_7_p17, slice_block_7_p18
  // slice_block slice_block_8: pin names not known; wires that end beside it: connection_box_23_p10, connection_box_23_p8, connection_box_23_p6, connection_box_23_p3, switch_block_47_r, switch_block_43_r, switch_block_39_r, switch_block_46_r, switch_block_47_r, d5, switch_block_42_r, switch_block_43_r, switch_block_38_r, switch_block_39_r, clk, switch_block_34_r, slice_block_8_p17
  // slice_block slice_block_9: pin names not known; wires that end beside it: connection_box_25_p10, connection_box_25_p8, connection_box_25_p6, connection_box_25_p3, switch_block_48_r, switch_block_44_r, switch_block_40_r, switch_block_47_r, slice_block_9_p9, d8, switch_block_43_r, slice_block_9_p12, switch_block_39_r, clk, switch_block_35_r, slice_block_9_p16
  // connection_box connection_box_27: pin names not known; wires that end beside it: switch_block_48_r, switch_block_44_r, switch_block_40_r, switch_block_36_r, clk, c10, p10, slice_block_9_p9, slice_block_9_p12, connection_box_27_p10, connection_box_27_p11
  // connection_box connection_box_28: pin names not known; wires that end beside it: switch_block_45_r, switch_block_41_r, switch_block_37_r, p19, c19, clk, connection_box_28_p7, slice_block_7_p12, slice_block_7_p14, connection_box_28_p10
  // connection_box connection_box_29: pin names not known; wires that end beside it: connection_box_28_p7, slice_block_7_p12, slice_block_7_p14, connection_box_28_p10, p18, c18, clk, connection_box_29_p8, connection_box_29_p9, connection_box_29_p10, slice_block_7_p17
  // connection_box connection_box_30: pin names not known; wires that end beside it: connection_box_27_p10, connection_box_30_p2, slice_block_9_p9, slice_block_9_p12, connection_box_27_p10, connection_box_27_p11, clk, c11, p11, connection_box_30_p10, connection_box_30_p11, connection_box_30_p12, connection_box_30_p2
  switch_block switch_block_49 (.L(slice_block_7_p17), .D(switch_block_49_d), .clk(clk), .cfg(s33));  // open: R, U
  // connection_box connection_box_31: pin names not known; wires that end beside it: slice_block_7_p18, switch_block_49_d, connection_box_31_p3, connection_box_31_p3, connection_box_31_p5, connection_box_31_p5, connection_box_31_p7, c28, clk, clk, connection_box_31_p11, connection_box_31_p12, connection_box_31_p12, connection_box_31_p14
  // connection_box connection_box_32: pin names not known; wires that end beside it: switch_block_34_r, connection_box_32_p2, connection_box_32_p2, connection_box_31_p7, connection_box_32_p5, c29, connection_box_32_p7, connection_box_32_p8
  switch_block switch_block_50 (
    .L(switch_block_34_r), .U(connection_box_32_p5), .D(switch_block_50_d), .clk(clk), .cfg(s73));  // open: R
  // connection_box connection_box_33: pin names not known; wires that end beside it: slice_block_8_p17, switch_block_50_d, connection_box_33_p3, connection_box_33_p3, connection_box_33_p5, connection_box_33_p5, connection_box_33_p7, c34, clk, clk, connection_box_33_p11, connection_box_33_p12, connection_box_33_p12, connection_box_33_p14
  // connection_box connection_box_34: pin names not known; wires that end beside it: switch_block_35_r, connection_box_34_p2, connection_box_34_p2, connection_box_33_p7, connection_box_34_p5, c35, connection_box_34_p7, connection_box_34_p8
  switch_block switch_block_51 (
    .L(switch_block_35_r), .U(connection_box_34_p5), .D(switch_block_51_d), .clk(clk), .cfg(s113));  // open: R
  // connection_box connection_box_35: pin names not known; wires that end beside it: slice_block_9_p16, switch_block_51_d, connection_box_35_p3, connection_box_35_p3, connection_box_35_p5, connection_box_35_p5, connection_box_35_p7, c40, clk, clk, connection_box_35_p11, connection_box_35_p12, connection_box_35_p12, connection_box_35_p14
  // connection_box connection_box_36: pin names not known; wires that end beside it: connection_box_36_p1, connection_box_36_p1, connection_box_35_p7, connection_box_36_p4, c41, connection_box_36_p6, connection_box_36_p7
  switch_block switch_block_52 (
    .L(connection_box_30_p2), .U(connection_box_36_p4), .clk(clk), .cfg(s153));  // open: R, D
  switch_block switch_block_53 (
    .L(connection_box_29_p10), .D(connection_box_31_p11), .clk(clk), .cfg(s32));  // open: R, U
  switch_block switch_block_54 (
    .L(switch_block_38_r), .U(connection_box_32_p8), .D(connection_box_33_p11), .clk(clk), .cfg(s72));  // open: R
  switch_block switch_block_55 (
    .L(switch_block_39_r), .U(connection_box_34_p8), .D(connection_box_35_p11), .clk(clk), .cfg(s112));  // open: R
  switch_block switch_block_56 (
    .L(connection_box_30_p12), .U(connection_box_36_p7), .clk(clk), .cfg(s152));  // open: R, D
  switch_block switch_block_57 (
    .L(connection_box_29_p9), .D(connection_box_31_p14), .clk(clk), .cfg(s31));  // open: R, U
  switch_block switch_block_58 (
    .L(switch_block_42_r), .U(switch_block_58_u), .D(connection_box_33_p14), .clk(clk), .cfg(s71));  // open: R
  switch_block switch_block_59 (
    .L(switch_block_43_r), .U(switch_block_59_u), .D(connection_box_35_p14), .clk(clk), .cfg(s111));  // open: R
  switch_block switch_block_60 (.L(connection_box_30_p11), .U(switch_block_60_u), .clk(clk), .cfg(s151));  // open: R, D
  switch_block switch_block_61 (.L(connection_box_29_p8), .D(switch_block_61_d), .clk(clk), .cfg(s30));  // open: R, U
  switch_block switch_block_62 (
    .L(switch_block_46_r), .U(switch_block_62_u), .D(switch_block_62_d), .clk(clk), .cfg(s70));  // open: R
  switch_block switch_block_63 (
    .L(switch_block_47_r), .U(switch_block_63_u), .D(switch_block_63_d), .clk(clk), .cfg(s110));  // open: R
  switch_block switch_block_64 (.L(connection_box_30_p10), .U(switch_block_64_u), .clk(clk), .cfg(s150));  // open: R, D
  // connection_box connection_box_37: pin names not known; wires that end beside it: connection_box_37_p1, connection_box_37_p1, connection_box_37_p3, connection_box_37_p3, connection_box_37_p5, connection_box_37_p5, clk, c17, switch_block_61_d, connection_box_37_p10, connection_box_37_p10, connection_box_37_p12, connection_box_37_p12, p17
  // connection_box connection_box_38: pin names not known; wires that end beside it: connection_box_32_p7, connection_box_38_p2, connection_box_38_p2, switch_block_58_u, c16, clk, connection_box_38_p7, connection_box_38_p7, switch_block_62_u, p16
  // connection_box connection_box_39: pin names not known; wires that end beside it: connection_box_39_p1, connection_box_39_p1, connection_box_39_p3, connection_box_39_p3, connection_box_39_p5, connection_box_39_p5, clk, c15, switch_block_62_d, connection_box_39_p10, connection_box_39_p10, connection_box_39_p12, connection_box_39_p12, p15
  // connection_box connection_box_40: pin names not known; wires that end beside it: connection_box_34_p7, connection_box_40_p2, connection_box_40_p2, switch_block_59_u, c14, clk, connection_box_40_p7, connection_box_40_p7, switch_block_63_u, p14
  // connection_box connection_box_41: pin names not known; wires that end beside it: connection_box_41_p1, connection_box_41_p1, connection_box_41_p3, connection_box_41_p3, connection_box_41_p5, connection_box_41_p5, clk, c13, switch_block_63_d, connection_box_41_p10, connection_box_41_p10, connection_box_41_p12, connection_box_41_p12, p13
  // connection_box connection_box_42: pin names not known; wires that end beside it: connection_box_36_p6, connection_box_42_p2, connection_box_42_p2, switch_block_60_u, c12, clk, connection_box_42_p7, connection_box_42_p7, switch_block_64_u, p12

  // Notes on the sheet:
  //   contents of io_cfg (hex, n*v repeats v):
  //   dfffff
  //   contents of sw_cfg0 (hex, n*v repeats v):
  //   4000000
  //   contents of sw_cfg2 (hex, n*v repeats v):
  //   80
  //   sw_cfg4 loads sw_data_cfg_4.hex
  //   sw_cfg6 loads sw_data_cfg_6.hex
  //   sw_cfg1 loads sw_data_cfg_1.hex
  //   sw_cfg3 loads sw_data_cfg_3.hex
  //   sw_cfg5 loads sw_data_cfg_5.hex
  //   sw_cfg7 loads sw_data_cfg_7.hex
  //   contents of conn_cfg0 (hex, n*v repeats v):
  //   848
  //   contents of conn_cfg1 (hex, n*v repeats v):
  //   10100000000
  //   conn_cfg2 loads conn_box_data_cfg_2.hex
  //   contents of slice_cfg0 (hex, n*v repeats v):
  //   10000803
  //   slice_cfg1 loads clb_data_cfg_1.hex
  //   slice_cfg2 loads clb_data_cfg_2.hex
  //   slice_cfg3 loads clb_data_cfg_3.hex
  //   slice_cfg4 loads clb_data_cfg_4.hex
  //   slice_cfg5 loads clb_data_cfg_5.hex
  //   slice_cfg6 loads clb_data_cfg_6.hex
  //   slice_cfg7 loads clb_data_cfg_7.hex
  //   slice_cfg8 loads clb_data_cfg_8.hex
endmodule
