// Digital circuit johnson_counter.dig as structural Verilog
module johnson_counter (
  input  clk,
  output Q0,
  output Q1,
  output Q2,
  output Q3
);

  fpga_ckt fpga_ckt_1 ();  // open: clk, p0, p1, p2, p3, p4, p5, p6, p7, p8, p9, p10, p11, p12, p13, p14, p15, p16, p17, p18, p19, p20, p21, p22, p23

  // Notes on the sheet:
  //   clk: Hz: 10
endmodule
