// Digital circuit mux41.dig as structural Verilog
module mux41 (
  input  clk,
  input  A0,
  input  A1,
  input  A2,
  input  A3,
  input  s1,
  input  s0,
  output Y
);

  // fpga_ckt fpga_ckt_1: pin names not known; wires that end beside it: A0, A1, A2, A3, s1, s0, clk, Y
endmodule
