// Digital circuit slice_block.dig as structural Verilog
module slice_block (
  input  A0,
  input  A3,
  input  A1,
  input  A2,
  input  B0,
  input  B1,
  input  B2,
  input  B3,
  input  C0,
  input  C1,
  input  C2,
  input  C3,
  input  clk0,
  input  clk1,
  input  clk2,
  input  clk,
  input  [32:0] cfg,
  output Y1,
  output Y2
);

  wire a_used, b_used, c_used, d_ff_1_q, d_ff_2_q, edge1, edge2, multiplexer_1_out, multiplexer_2_out,
       multiplexer_3_out, multiplexer_4_out, multiplexer_8_out, multiplexer_9_out, multiplexer_10_out,
       multiplexer_11_out, multiplexer_12_out, multiplexer_13_out, not_1_out;
  wire [2:0] multiplexer_5_out;
  wire [7:0] data1, data2, register_2_q, register_3_q;
  wire [11:0] register_1_q;

  Register #(.Bits(33)) register_1 (
    .D(cfg), .C(clk), .en(1'b1), .Q({data2, data1, c_used, b_used, a_used, edge2, edge1, register_1_q}));
  Multiplexer #(.Selector_Bits(2)) multiplexer_1 (
    .sel(register_1_q[7:6]), .in_0(A0), .in_1(A1), .in_2(A2), .in_3(A3), .out(multiplexer_1_out));
  Multiplexer #(.Selector_Bits(2)) multiplexer_2 (
    .sel(register_1_q[5:4]), .in_0(B0), .in_1(B1), .in_2(B2), .in_3(B3), .out(multiplexer_2_out));
  Multiplexer #(.Selector_Bits(2)) multiplexer_3 (
    .sel(register_1_q[3:2]), .in_0(C0), .in_1(C1), .in_2(C2), .in_3(C3), .out(multiplexer_3_out));
  Multiplexer #(.Selector_Bits(2)) multiplexer_4 (
    .sel(register_1_q[1:0]), .in_0(clk0), .in_1(clk1), .in_2(clk2), .in_3(clk), .out(multiplexer_4_out));
  Multiplexer multiplexer_5 (.sel(a_used), .in_0(1'b0), .in_1(multiplexer_1_out), .out(multiplexer_5_out[2]));
  Multiplexer multiplexer_6 (.sel(b_used), .in_0(1'b0), .in_1(multiplexer_2_out), .out(multiplexer_5_out[1]));
  Multiplexer multiplexer_7 (.sel(c_used), .in_0(1'b0), .in_1(multiplexer_3_out), .out(multiplexer_5_out[0]));
  Register #(.Bits(8)) register_2 (.D(data1), .C(clk), .en(1'b1), .Q(register_2_q));
  Register #(.Bits(8)) register_3 (.D(data2), .C(clk), .en(1'b1), .Q(register_3_q));
  Multiplexer #(.Selector_Bits(3)) multiplexer_8 (
    .sel(multiplexer_5_out), .in_0(register_2_q[0]), .in_1(register_2_q[1]), .in_2(register_2_q[2]),
    .in_3(register_2_q[3]), .in_4(register_2_q[4]), .in_5(register_2_q[5]), .in_6(register_2_q[6]),
    .in_7(register_2_q[7]), .out(multiplexer_8_out));
  not not_1 (not_1_out, multiplexer_4_out);
  Multiplexer #(.Selector_Bits(3)) multiplexer_9 (
    .sel(multiplexer_5_out), .in_0(register_3_q[0]), .in_1(register_3_q[1]), .in_2(register_3_q[2]),
    .in_3(register_3_q[3]), .in_4(register_3_q[4]), .in_5(register_3_q[5]), .in_6(register_3_q[6]),
    .in_7(register_3_q[7]), .out(multiplexer_9_out));
  Multiplexer multiplexer_10 (.sel(edge1), .in_0(multiplexer_4_out), .in_1(not_1_out), .out(multiplexer_10_out));
  Multiplexer multiplexer_11 (.sel(edge2), .in_0(multiplexer_4_out), .in_1(not_1_out), .out(multiplexer_11_out));
  D_FF d_ff_1 (.D(multiplexer_8_out), .C(multiplexer_10_out), .Q(d_ff_1_q));  // open: nQ
  D_FF d_ff_2 (.D(multiplexer_9_out), .C(multiplexer_11_out), .Q(d_ff_2_q));  // open: nQ
  Multiplexer multiplexer_12 (
    .sel(register_1_q[8]), .in_0(multiplexer_8_out), .in_1(d_ff_1_q), .out(multiplexer_12_out));
  Multiplexer multiplexer_13 (
    .sel(register_1_q[9]), .in_0(multiplexer_9_out), .in_1(d_ff_2_q), .out(multiplexer_13_out));
  assign Y1 = register_1_q[10] ? multiplexer_12_out : 1'bz;  // Driver driver_1
  assign Y2 = register_1_q[11] ? multiplexer_13_out : 1'bz;  // Driver driver_2
endmodule
