// Digital circuit switch_block.dig as structural Verilog
module switch_block (
  input  clk,
  input  Si,
  output R,
  output L,
  output U,
  output D,
  output So
);

  wire s1, s2, s3, s4, s5, s6, shift_reg_4bit_1_o;
  wire [3:2] shift_reg_4bit_2_d;

  shift_reg_4bit shift_reg_4bit_1 (.i(Si), .c(clk), .o(shift_reg_4bit_1_o), .d({s4, s3, s2, s1}));
  shift_reg_4bit shift_reg_4bit_2 (.i(shift_reg_4bit_1_o), .c(clk), .o(So), .d({shift_reg_4bit_2_d, s6, s5}));
  NFET nfet_1 (.G(s1), .D(U), .S(L));
  NFET nfet_2 (.G(s4), .D(L), .S(D));
  NFET nfet_3 (.G(s5), .D(R), .S(L));
  NFET nfet_4 (.G(s6), .D(U), .S(D));
  NFET nfet_5 (.G(s2), .D(R), .S(U));
  NFET nfet_6 (.G(s3), .D(D), .S(R));
endmodule
